// Logisim project 505.circ as structural Verilog: 1 circuit, main circuit main
module main (
  input  x1,
  input  x2,
  input  x3
);

  wire and_1_out, and_2_out, and_3_out, and_4_out, and_5_out, and_6_out, not_1_out, not_2_out, not_3_out,
       xor_1_out, xor_2_out, xor_3_out;

  not not_1 (not_1_out, x1);
  not not_2 (not_2_out, x2);
  not not_3 (not_3_out, x3);
  and and_1 (and_1_out, x1, not_3_out, not_2_out);
  xor xor_1 (xor_1_out, x3, x1);
  and and_2 (and_2_out, not_1_out, x2, not_3_out);
  LED led_1 (.in(and_1_out));
  xor xor_2 (xor_2_out, x2, x3);
  xor xor_3 (xor_3_out, x2, x1);
  and and_3 (and_3_out, not_3_out, x2, not_1_out);
  LED led_2 (.in(and_3_out));
  LED led_3 (.in(and_2_out));
  and and_4 (and_4_out, xor_2_out, not_1_out);
  and and_5 (and_5_out, xor_3_out, not_2_out);
  LED led_4 (.in(and_6_out));
  and and_6 (and_6_out, not_2_out, xor_1_out);
  LED led_5 (.in(and_4_out));
  LED led_6 (.in(and_5_out));

  // Notes on the sheet:
  //   y1
  //   y4
  //   y6
  //   y2
  //   y3
  //   y5
endmodule
